// Logisim project 1° Laboratório e Exercícios de Simulação (Mateus Henrique).circ as structural Verilog
module _1___S____A___B____B___C (
  input  A,
  input  B,
  input  C,
  output out_4
);

  wire not_1_out, or_1_out, or_2_out;

  not not_1 (not_1_out, B);
  or or_1 (or_1_out, A, B);
  or or_2 (or_2_out, not_1_out, C);
  and and_1 (out_4, or_1_out, or_2_out);
endmodule

module _2___S___A_C_____B_C_____A_B_C (
  input  A,
  input  B,
  input  C,
  output S
);

  wire and_1_out, and_2_out, nand_1_out, not_1_out;

  and and_1 (and_1_out, A, C);
  nand nand_1 (nand_1_out, B, C);
  not not_1 (not_1_out, A);
  and and_2 (and_2_out, not_1_out, B, C);
  or or_1 (S, and_1_out, nand_1_out, and_2_out);
endmodule

module _3___S___A_B____C_____C_D (
  input  A,
  input  B,
  input  C,
  input  D,
  output S
);

  wire and_1_out, nand_1_out, not_1_out;

  and and_1 (and_1_out, A, B);
  not not_1 (not_1_out, C);
  nand nand_1 (nand_1_out, C, D);
  or or_1 (S, and_1_out, not_1_out, nand_1_out);
endmodule

module _4___Z___X___Y___W (
  input  X,
  input  Y,
  input  W,
  output Z
);

  wire not_1_out, or_1_out;

  not not_1 (not_1_out, Y);
  or or_1 (or_1_out, not_1_out, W);
  and and_1 (Z, X, or_1_out);
endmodule

module \Exercício_2_Construir_e_simular_o_circuito_Ou_Exclusivo_com_portas_AND__OR_e_NOT__conforme_a_figura  (
  input  A,
  input  B,
  output S
);

  wire and_1_out, and_2_out, not_1_out, not_2_out;

  not not_1 (not_1_out, A);
  not not_2 (not_2_out, B);
  and and_1 (and_1_out, not_1_out, B);
  and and_2 (and_2_out, A, not_2_out);
  or or_1 (S, and_1_out, and_2_out);

  // Notes on the sheet:
  //   S =~A.B +  A.B
endmodule
