// Logisim project 2° Circuitos envolvendo somador e negador disponíveis no Logisim..circ as structural Verilog: 7 circuits, main circuit 1.Construir o circuito Meio Somador e o Somador Completo no Logisim.
module _1_Construir_o_circuito_Meio_Somador_e_o_Somador_Completo_no_Logisim (
  input  in_1,
  input  in_2,
  input  in_3,
  input  in_4,
  input  in_5,
  output out_6,
  output out_7,
  output out_8,
  output out_9
);

  wire and_2_out, and_3_out, xor_1_out;

  xor xor_1 (xor_1_out, in_4, in_5);
  and and_1 (out_6, in_2, in_1);
  xor xor_2 (out_7, in_1, in_2);
  and and_2 (and_2_out, in_5, in_4);
  and and_3 (and_3_out, in_3, xor_1_out);
  xor xor_3 (out_9, in_3, xor_1_out);
  or or_1 (out_8, and_2_out, and_3_out);

  // Notes on the sheet:
  //   Circuito Meio Somador
  //   Circuito Somador completo
  //   1. Construir o circuito Meio Somador e o Somador completo no Logisim.
endmodule

module _2_Construir_um_somador_de_4_bits__interligando_somadores_de_1_bit_do_Logisim (
  input  in_1,
  input  in_2,
  input  in_3,
  input  in_4,
  input  in_5,
  input  in_6,
  input  in_7,
  input  in_8,
  output out_9,
  output out_10,
  output out_11,
  output out_12,
  output out_13
);

  wire adder_1_cout, adder_1_out, adder_2_cout, adder_2_out, adder_3_cout, adder_3_out, adder_4_out;

  Adder #(.width(1)) adder_1 (.a(in_1), .b(in_2), .out(adder_1_out), .cout(adder_1_cout));  // open: cin
  Adder #(.width(1)) adder_2 (.a(in_3), .b(in_4), .out(adder_2_out), .cin(adder_1_cout), .cout(adder_2_cout));
  Adder #(.width(1)) adder_3 (.a(in_5), .b(in_6), .out(adder_3_out), .cin(adder_2_cout), .cout(adder_3_cout));
  Adder #(.width(1)) adder_4 (.a(in_7), .b(in_8), .out(adder_4_out), .cin(adder_3_cout), .cout(out_9));

  // Notes on the sheet:
  //   2.Construir um somador de 4 bits, interligados somadores de 1 bit do Logisim.
endmodule

module \_3_Construir_um_somador_de_4_bits_com_um_único_somador_do_Logisim  (
  input  [3:0] in_1,
  input  [3:0] in_2,
  output [3:0] out_3,
  output out_4
);

  Adder #(.width(4)) adder_1 (.a(in_1), .b(in_2), .out(out_3), .cout(out_4));  // open: cin

  // Notes on the sheet:
  //   3.Construir um simulador  de 4 bits, com um único somodar do Logísim.
endmodule

module _4_Construir_e_simular_um_somador_de_8_bits__interligando_dois_somadores_de_4_bits (
  input  [3:0] in_1,
  input  [3:0] in_2,
  input  [3:0] in_3,
  input  [3:0] in_4,
  output [3:0] out_5,
  output [3:0] out_6,
  output out_7
);

  wire adder_1_cout;

  Adder #(.width(4)) adder_1 (.a(in_1), .b(in_2), .out(out_5), .cout(adder_1_cout));  // open: cin
  Adder #(.width(4)) adder_2 (.a(in_3), .b(in_4), .out(out_6), .cin(adder_1_cout), .cout(out_7));

  // Notes on the sheet:
  //   4. Construir e simular um somador  de 8 bits, interligado dois somadores de 4 bits.
endmodule

module _5_Construir_e_simular_um_subtrator_de_4_bits (
  input  [3:0] in_1,
  input  [3:0] in_2,
  output [3:0] out_3
);

  Subtractor #(.width(4)) subtractor_1 (.a(in_1), .b(in_2), .out(out_3));  // open: bin, bout

  // Notes on the sheet:
  //   5.Construir e simular um subtrator de 4 bits.
endmodule

module \_6_Construir_e_simular_um_negador_de_4_bits__Comparar_resultados_de_saída_com_as_conversões_em_complemento_de_2  (
  input  [3:0] in_1,
  output [3:0] out_2
);

  Negator #(.width(4)) negator_1 (.in(in_1), .out(out_2));

  // Notes on the sheet:
  //   6.Construir e simular um negador de 4 bits.
endmodule

module \_7_Construir_um_circuito_para_subtrair_dois_binários_de_4_bits_usando_um_somador_e_um_negador_de_4_bits__Comparar_os_resultados_com_o_subtrator_de_4_bits  (
  input  [3:0] in_1,
  input  [3:0] in_2,
  output [3:0] out_3
);

  wire [3:0] negator_1_out;

  Negator #(.width(4)) negator_1 (.in(in_2), .out(negator_1_out));
  Adder #(.width(4)) adder_1 (.a(in_1), .b(negator_1_out), .out(out_3));  // open: cin, cout

  // Notes on the sheet:
  //   7.Construir um circuito para subtrair dois binários de 4 bits usando um somador e um negador de 4 bits.
endmodule
