// Logisim project 3° Decodificador Mateus Henrique..circ as structural Verilog
module \Exercícios  (
);


  // Notes on the sheet:
  //   Resposta:  29 Linhas de endereço.
  //   Resposta: 32 Linhas de endereço.
  //   1.Para que o computador acesse uma memória RAM de 512 Mi(Mibi ou Mega) Bytes, quantas linhas de endereço ele precisa ter? 
  //   3.Pesquise sobre a capacidade de expansão de memória RAM dos computadores pessoais modernos.
  //   Resposta: Os computadores modernos de 64 bit gerenciam até 128 GB de memória RAM e 16 TB de memória virtual
  //   2. Se o computador tem um limite de expansão da memória RAM de 4 Gi(Giga ou Gibi)Bytes, quantas linhas de endereço de memória ele possui?
endmodule

module \_1_Construír_com_portas_lógicas_um_circuito_decodificador_de_2_bits_de_entrada_e_1_de_4_saídas  (
  input  A1,
  input  A0,
  output D0,
  output D1,
  output D2,
  output D3
);

  and and_1 (D0, ~A1, ~A1);  // AND_Gate
  and and_2 (D1, A1, ~A1);  // AND_Gate
  and and_3 (D2, ~A1, A1);  // AND_Gate
  and and_4 (D3, A0, A1);

  // Notes on the sheet:
  //   1.Construir com portas lógicas um circuito decodificador de 2 bits de entrada e 1 de 4 saídas.
endmodule

module \_2__Construír_com_portas_lógicas_um_circuito_decodificador_de_3_bits_de_entrada_e_1_de_8_saídas  (
  input  A2,
  input  A1,
  input  A0,
  output out_4,
  output out_5,
  output out_6,
  output out_7,
  output out_8,
  output out_9,
  output out_10,
  output out_11
);

  and and_1 (out_4, ~A0, ~A1, ~A2);  // AND_Gate
  and and_2 (out_5, A0, ~A1, ~A2);  // AND_Gate
  and and_3 (out_6, ~A0, A1, ~A2);  // AND_Gate
  and and_4 (out_7, A0, A1, ~A2);  // AND_Gate
  and and_5 (out_8, ~A0, ~A1, A2);  // AND_Gate
  and and_6 (out_9, A0, ~A1, A2);  // AND_Gate
  and and_7 (out_10, ~A0, A1, A2);  // AND_Gate
  and and_8 (out_11, A0, A1, A2);

  // Notes on the sheet:
  //   2.Construir com portas lógicas um circuito decodificador de 3 bits de entrada e 1 de 8 saídas.
endmodule

module \_3__Construir_e_simular_um_decodificador_de_2_bits_de_entrada_e_1_de_4_saídas_a_partir_do_módulo_decodificador_disponível_no_Logisim  (
  input  [1:0] in_1,
  output out_2,
  output out_3,
  output out_4,
  output out_5
);

  Decoder #(.select(2)) decoder_1 (.out0(out_2), .out1(out_3), .out2(out_4), .out3(out_5), .sel(in_1));  // open: en

  // Notes on the sheet:
  //   3. Construir e simular um decodificador de 2 bits de entrada e 1 de 4 saídas a partir do módulo decodificador disponível no Logisim.
endmodule

module \_4__Modificar_o_circuito_para_que_funcione_como_decodificador_de_3_bits_de_entrada_e_1_de_8_saídas  (
  input  [2:0] in_1,
  output out_2,
  output out_3,
  output out_4,
  output out_5,
  output out_6,
  output out_7,
  output out_8,
  output out_9
);

  Decoder #(.select(3)) decoder_1 (
    .out0(out_2), .out1(out_3), .out2(out_4), .out3(out_5), .out4(out_6), .out5(out_7), .out6(out_8),
    .out7(out_9), .sel(in_1));  // open: en

  // Notes on the sheet:
  //   4. Modificar o circuito para que funcione como decodificador de 3 bits de entrada e 1 de 8 saídas
endmodule
