// Logisim project 5° Relógio Logisim(Mateus Henrique).circ as structural Verilog: 1 circuit, main circuit Projeto Relógio no Logisim
module \Projeto_Relógio_no_Logisim  (
  output [3:0] out_1,
  output out_2,
  output [3:0] out_3,
  output [3:0] out_4,
  output [3:0] out_5,
  output [3:0] out_6,
  output [3:0] out_7,
  output out_8
);

  wire and_1_out, and_2_out, and_3_out, button_1_out, clock_1_out, counter_1_carry, counter_2_carry,
       counter_3_carry, counter_4_carry, counter_5_carry;

  Hex_Digit_Display hex_digit_display_1 (.value(out_6), .dp(1'b1));
  Hex_Digit_Display hex_digit_display_2 (.value(out_7));  // open: dp
  LED led_1 (.in(1'b1));
  LED led_2 (.in(1'b1));
  Hex_Digit_Display hex_digit_display_3 (.value(out_5));  // open: dp
  LED led_3 (.in(1'b1));
  LED led_4 (.in(1'b1));
  Hex_Digit_Display hex_digit_display_4 (.value(out_4), .dp(1'b1));
  Hex_Digit_Display hex_digit_display_5 (.value(out_1));  // open: dp
  Hex_Digit_Display hex_digit_display_6 (.value(out_3));  // open: dp
  Counter #(.width(4), .max('h5)) counter_1 (
    .Q(out_3), .carry(counter_1_carry), .clk(counter_5_carry));  // open: load, D, count, clr
  Counter #(.width(4), .max('h9)) counter_2 (
    .Q(out_4), .carry(counter_2_carry), .clk(counter_1_carry));  // open: load, D, count, clr
  Counter #(.width(4), .max('h5)) counter_3 (
    .Q(out_5), .carry(counter_3_carry), .clk(counter_2_carry));  // open: load, D, count, clr
  Counter #(.width(4), .max('h9)) counter_4 (
    .Q(out_6), .carry(counter_4_carry), .clk(counter_3_carry), .clr(out_2));  // open: load, D, count
  Counter #(.width(4), .max('h9)) counter_5 (
    .Q(out_1), .carry(counter_5_carry), .clk(clock_1_out));  // open: load, D, count, clr
  Clock clock_1 (.out(clock_1_out));
  Counter #(.width(4), .max('h2)) counter_6 (
    .Q(out_7), .carry(out_8), .clk(counter_4_carry), .clr(out_2));  // open: load, D, count
  LED led_5 (.in(and_1_out));
  buf and_1 (and_1_out, button_1_out);  // AND_Gate
  Button button_1 (.out(button_1_out));
  buf and_2 (and_2_out, out_6[2]);  // AND_Gate
  buf and_3 (and_3_out, out_7[1]);  // AND_Gate
  and and_4 (out_2, and_2_out, and_3_out);
endmodule
